// Logisim project Lab 7.circ as structural Verilog: 22 circuits, main circuit main
module main (
);

  wire CLK, Down, Left, MemWrite, RDSel, Right, Up, WELED, WEM;
  wire [7:0] Pressed;
  wire [31:0] Instr, MemAddr, PC, ReadData, ReadDataM, WriteData;
  wire [63:0] A, B, C, D;

  Clock clock_1 (.out(CLK));
  // DotMatrix #(.inputtype("row"), .matrixcols(16), .matrixrows(16)) dotmatrix_1: pin names not known; wires that end beside it: A[63:48], A[47:32], A[31:16], A[15:0], B[63:48], B[47:32], B[31:16], B[15:0], C[63:48], C[47:32], C[31:16], C[15:0], D[63:48], D[47:32], D[31:16], D[15:0]
  // Probe on Instr
  // Probe on ReadData
  // Probe on MemWrite
  // Probe on MemAddr
  Button button_1 (.out(Up));
  Button button_2 (.out(Left));
  Button button_3 (.out(Down));
  // Probe on PC
  Button button_4 (.out(Right));
  // Probe on Instr
  instmem instmem_1 (.Address(PC), .Instr(Instr));
  // Probe on WEM
  addressdecoder addressdecoder_1 (.MemWrite(MemWrite), .MemAddr(MemAddr), .WEM(WEM), .WELED(WELED), .RDSel(RDSel));
  // Probe on WELED
  // Probe on RDSel
  // Probe on PC
  // Probe on MemWrite
  scp scp_1 (
    .CLK(CLK), .Instr(Instr), .ReadData(ReadData), .PC(PC), .MemWrite(MemWrite), .MemAddr(MemAddr),
    .WriteData(WriteData));
  // Probe on MemAddr
  // Probe on WriteData
  // Probe on MemAddr
  // Probe on MemAddr[7:0]
  // Probe on WriteData[0]
  // Probe on WELED
  // Probe on MemAddr
  // Probe on WriteData
  // Probe on ReadDataM
  // Probe on {{24{1'b0}}, Pressed}
  // Probe on RDSel
  // Probe on WEM
  memory memory_1 (.A(MemAddr), .WD(WriteData), .CLK(CLK), .WE(WEM), .ReadData(ReadDataM));
  Multiplexer #(.enable("true"), .width(32)) multiplexer_1 (
    .in0(ReadDataM), .in1({{24{1'b0}}, Pressed}), .out(ReadData), .sel(RDSel));  // open: en
  // Probe on ReadDataM
  keypadcontroller keypadcontroller_1 (
    .CLK(CLK), .Up(Up), .Down(Down), .Left(Left), .Right(Right), .Read(RDSel), .Pressed(Pressed));
  ledmatrixcontroller ledmatrixcontroller_1 (
    .CLK(CLK), .Address(MemAddr[7:0]), .WriteBit(WriteData[0]), .WE(WELED), .A(A), .B(B), .C(C), .D(D));
  // Probe on {{24{1'b0}}, Pressed}
endmodule

module addressdecoder (
  input  MemWrite,
  input  [31:0] MemAddr,
  output WEM,
  output WELED,
  output RDSel
);

  wire and_1_out, comparator_2_eq, comparator_2_gt, comparator_3_eq, comparator_3_lt, not_1_out, or_1_out,
       or_2_out;

  Comparator #(.mode("unsigned"), .width(32)) comparator_1 (.a(MemAddr), .b(32'h300), .eq(RDSel));  // open: gt, lt
  Comparator #(.mode("unsigned"), .width(32)) comparator_2 (
    .a(MemAddr), .b(32'h200), .gt(comparator_2_gt), .eq(comparator_2_eq));  // open: lt
  Comparator #(.mode("unsigned"), .width(32)) comparator_3 (
    .a(MemAddr), .b(32'h2ff), .eq(comparator_3_eq), .lt(comparator_3_lt));  // open: gt
  or or_1 (or_1_out, comparator_2_gt, comparator_2_eq);
  and and_1 (and_1_out, or_1_out, or_2_out);
  or or_2 (or_2_out, comparator_3_eq, comparator_3_lt);
  not not_1 (not_1_out, and_1_out);
  and and_2 (WELED, and_1_out, MemWrite);
  and and_3 (WEM, not_1_out, MemWrite);
endmodule

module keypadcontroller (
  input  CLK,
  input  Up,
  input  Down,
  input  Left,
  input  Right,
  input  Read,
  output [7:0] Pressed
);

  wire CLR, or_1_out, WE;

  reg1 reg1_1 (.WE(1'b1), .CLK(CLK), .in_1(Read), .out_5(CLR));  // open: CLR
  or or_1 (or_1_out, Pressed[0], Pressed[1], Pressed[2], Pressed[3]);
  not not_1 (WE, or_1_out);
  reg1 reg1_2 (.WE(WE), .CLK(CLK), .CLR(CLR), .in_1(Up), .out_5(Pressed[0]));
  reg1 reg1_3 (.WE(WE), .CLK(CLK), .CLR(CLR), .in_1(Down), .out_5(Pressed[1]));
  reg1 reg1_4 (.WE(WE), .CLK(CLK), .CLR(CLR), .in_1(Left), .out_5(Pressed[2]));
  reg1 reg1_5 (.WE(WE), .CLK(CLK), .CLR(CLR), .in_1(Right), .out_5(Pressed[3]));

  assign Pressed[7:4] = 4'b0000;

  // Other names for the same wires on the sheet: U = Pressed[0]; D = Pressed[1]; L = Pressed[2]; R = Pressed[3]
endmodule

module ledmatrixcontroller (
  input  CLK,
  input  [7:0] Address,
  input  WriteBit,
  input  WE,
  output [63:0] A,
  output [63:0] B,
  output [63:0] C,
  output [63:0] D
);

  bitarray256 bitarray256_1 (
    .WriteBit(WriteBit), .CLK(CLK), .WE(WE), .BitAddr(Address), .DataOut1(B), .DataOut2(C), .DataOut3(D),
    .DataOut0(A));
endmodule

module bitarray8 (
  input  [2:0] BitAddr,
  input  WriteBit,
  input  CLK,
  input  WE,
  output [7:0] out_5
);

  wire decoder_1_out0, decoder_1_out1, decoder_1_out2, decoder_1_out3, decoder_1_out4, decoder_1_out5,
       decoder_1_out6, decoder_1_out7;

  Decoder #(.select(3)) decoder_1 (
    .out0(decoder_1_out0), .out1(decoder_1_out1), .out2(decoder_1_out2), .out3(decoder_1_out3),
    .out4(decoder_1_out4), .out5(decoder_1_out5), .out6(decoder_1_out6), .out7(decoder_1_out7),
    .sel(BitAddr), .en(WE));
  reg1 reg1_1 (.WE(decoder_1_out0), .CLK(CLK), .in_1(WriteBit), .out_5(out_5[7]));  // open: CLR
  reg1 reg1_2 (.WE(decoder_1_out1), .CLK(CLK), .in_1(WriteBit), .out_5(out_5[6]));  // open: CLR
  reg1 reg1_3 (.WE(decoder_1_out2), .CLK(CLK), .in_1(WriteBit), .out_5(out_5[5]));  // open: CLR
  reg1 reg1_4 (.WE(decoder_1_out3), .CLK(CLK), .in_1(WriteBit), .out_5(out_5[4]));  // open: CLR
  reg1 reg1_5 (.WE(decoder_1_out4), .CLK(CLK), .in_1(WriteBit), .out_5(out_5[3]));  // open: CLR
  reg1 reg1_6 (.WE(decoder_1_out5), .CLK(CLK), .in_1(WriteBit), .out_5(out_5[2]));  // open: CLR
  reg1 reg1_7 (.WE(decoder_1_out6), .CLK(CLK), .in_1(WriteBit), .out_5(out_5[1]));  // open: CLR
  reg1 reg1_8 (.WE(decoder_1_out7), .CLK(CLK), .in_1(WriteBit), .out_5(out_5[0]));  // open: CLR

  // Other names for the same wires on the sheet: DataOut[7:0] = out_5; DataOut7 = out_5[0]; DataOut6 = out_5[1];
  //   DataOut5 = out_5[2]; DataOut4 = out_5[3]; DataOut3 = out_5[4]; DataOut2 = out_5[5]; DataOut1 = out_5[6];
  //   DataOut0 = out_5[7]
endmodule

module bitarray64 (
  input  [5:0] BitAddr,
  input  WriteBit,
  input  CLK,
  input  WE,
  output [63:0] out_5
);

  wire decoder_1_out0, decoder_1_out1, decoder_1_out2, decoder_1_out3, decoder_1_out4, decoder_1_out5,
       decoder_1_out6, decoder_1_out7;

  Decoder #(.select(3)) decoder_1 (
    .out0(decoder_1_out0), .out1(decoder_1_out1), .out2(decoder_1_out2), .out3(decoder_1_out3),
    .out4(decoder_1_out4), .out5(decoder_1_out5), .out6(decoder_1_out6), .out7(decoder_1_out7),
    .sel(BitAddr[5:3]), .en(WE));
  bitarray8 bitarray8_1 (
    .CLK(CLK), .WE(decoder_1_out0), .WriteBit(WriteBit), .BitAddr(BitAddr[2:0]), .out_5(out_5[63:56]));
  bitarray8 bitarray8_2 (
    .CLK(CLK), .WE(decoder_1_out1), .WriteBit(WriteBit), .BitAddr(BitAddr[2:0]), .out_5(out_5[55:48]));
  bitarray8 bitarray8_3 (
    .CLK(CLK), .WE(decoder_1_out2), .WriteBit(WriteBit), .BitAddr(BitAddr[2:0]), .out_5(out_5[47:40]));
  bitarray8 bitarray8_4 (
    .CLK(CLK), .WE(decoder_1_out3), .WriteBit(WriteBit), .BitAddr(BitAddr[2:0]), .out_5(out_5[39:32]));
  bitarray8 bitarray8_5 (
    .CLK(CLK), .WE(decoder_1_out4), .WriteBit(WriteBit), .BitAddr(BitAddr[2:0]), .out_5(out_5[31:24]));
  bitarray8 bitarray8_6 (
    .CLK(CLK), .WE(decoder_1_out5), .WriteBit(WriteBit), .BitAddr(BitAddr[2:0]), .out_5(out_5[23:16]));
  bitarray8 bitarray8_7 (
    .CLK(CLK), .WE(decoder_1_out6), .WriteBit(WriteBit), .BitAddr(BitAddr[2:0]), .out_5(out_5[15:8]));
  bitarray8 bitarray8_8 (
    .CLK(CLK), .WE(decoder_1_out7), .WriteBit(WriteBit), .BitAddr(BitAddr[2:0]), .out_5(out_5[7:0]));

  // Other names for the same wires on the sheet: Offset[2:0] = BitAddr[2:0]; BlockAddr[2:0] = BitAddr[5:3];
  //   DataOut[63:0] = out_5; DataOut7[7:0] = out_5[7:0]; DataOut6[7:0] = out_5[15:8]; DataOut5[7:0] = out_5[23:16];
  //   DataOut4[7:0] = out_5[31:24]; DataOut3[7:0] = out_5[39:32]; DataOut2[7:0] = out_5[47:40];
  //   DataOut1[7:0] = out_5[55:48]; DataOut0[7:0] = out_5[63:56]
endmodule

module bitarray256 (
  input  [7:0] BitAddr,
  input  WriteBit,
  input  CLK,
  input  WE,
  output [63:0] DataOut0,
  output [63:0] DataOut1,
  output [63:0] DataOut2,
  output [63:0] DataOut3
);

  wire decoder_1_out0, decoder_1_out1, decoder_1_out2, decoder_1_out3;

  Decoder #(.select(2)) decoder_1 (
    .out0(decoder_1_out0), .out1(decoder_1_out1), .out2(decoder_1_out2), .out3(decoder_1_out3),
    .sel(BitAddr[7:6]), .en(WE));
  bitarray64 bitarray64_1 (
    .WriteBit(WriteBit), .CLK(CLK), .WE(decoder_1_out0), .BitAddr(BitAddr[5:0]), .out_5(DataOut0));
  bitarray64 bitarray64_2 (
    .WriteBit(WriteBit), .CLK(CLK), .WE(decoder_1_out1), .BitAddr(BitAddr[5:0]), .out_5(DataOut1));
  bitarray64 bitarray64_3 (
    .WriteBit(WriteBit), .CLK(CLK), .WE(decoder_1_out2), .BitAddr(BitAddr[5:0]), .out_5(DataOut2));
  bitarray64 bitarray64_4 (
    .WriteBit(WriteBit), .CLK(CLK), .WE(decoder_1_out3), .BitAddr(BitAddr[5:0]), .out_5(DataOut3));

  // Other names for the same wires on the sheet: Offset[5:0] = BitAddr[5:0]; BlockAddr[1:0] = BitAddr[7:6]
endmodule

module scp (
  input  CLK,
  input  [31:0] Instr,
  input  [31:0] ReadData,
  output [31:0] PC,
  output MemWrite,
  output [31:0] MemAddr,
  output [31:0] WriteData
);

  wire ALUSrcBE, and_1_out, BranchD, JumpD, PCSrcE, RegWriteD, Zero, ZeroE;
  wire [1:0] ResultSrcD;
  wire [2:0] ALUControlD, ImmSrcD;
  wire [31:0] ImmExtD, NextPC, PCPlus4D, PCTargetE, RD1D, ResultW, SrcBE;

  // Probe on PCSrcE
  Multiplexer #(.width(32)) multiplexer_1 (.in0(PCPlus4D), .in1(PCTargetE), .out(NextPC), .sel(PCSrcE));
  // Probe on NextPC
  reg32 PCF (.CLK(CLK), .in_1(NextPC), .out_5(PC));  // open: WE, CLR
  Adder #(.width(32)) adder_1 (.a(PC), .b(32'h4), .out(PCPlus4D));  // open: cin, cout
  // Probe on Instr
  // Probe on PC
  // Probe on PCPlus4D
  // Probe on Instr
  // Probe on PC
  // Probe on PCPlus4D
  // Probe on Instr[6:0]
  // Probe on Instr[14:12]
  // Probe on Instr[30]
  // Probe on Zero
  // Digital_Oscilloscope #(.showclock("false")) digital_oscilloscope_1: pin names not known; wires that end beside it: CLK, CLK
  controlunit controlunit_1 (
    .funct3(Instr[14:12]), .funct7_5(Instr[30]), .opcode(Instr[6:0]), .RegWrite(RegWriteD),
    .ResultSrc(ResultSrcD), .MemWrite(MemWrite), .Jump(JumpD), .Branch(BranchD), .ALUControl(ALUControlD),
    .ALUSrc(ALUSrcBE), .ImmSrc(ImmSrcD));
  // Probe on Instr[19:15]
  // Probe on Instr[24:20]
  // Probe on Instr[11:7]
  // Probe on ResultW
  // Probe on ImmSrcD
  regfile regfile_1 (
    .A1(Instr[19:15]), .A2(Instr[24:20]), .A3(Instr[11:7]), .WD3(ResultW), .CLK(CLK), .WE3(RegWriteD),
    .RD1(RD1D), .RD2(WriteData));
  extend extend_1 (.Instr(Instr), .ImmSrc(ImmSrcD), .ImmExt(ImmExtD));
  // Probe on RegWriteD
  // Probe on ResultSrcD
  // Probe on MemWrite
  // Probe on JumpD
  // Probe on BranchD
  // Probe on ALUControlD
  // Probe on ALUSrcBE
  // Probe on RD1D
  // Probe on WriteData
  // Probe on PC
  // Probe on Instr[19:15]
  // Probe on Instr[24:20]
  // Probe on Instr[11:7]
  // Probe on ImmExtD
  // Probe on PCPlus4D
  // Probe on RegWriteD
  // Probe on ResultSrcD
  // Probe on MemWrite
  // Probe on JumpD
  // Probe on BranchD
  // Probe on ALUControlD
  // Probe on ALUSrcBE
  // Probe on RD1D
  // Probe on WriteData
  // Probe on PC
  // Probe on Instr[19:15]
  // Probe on Instr[24:20]
  // Probe on Instr[11:7]
  // Probe on ImmExtD
  // Probe on PCPlus4D
  or or_1 (PCSrcE, and_1_out, JumpD);
  and and_1 (and_1_out, ZeroE, BranchD);
  // Probe on ALUSrcBE
  Multiplexer #(.width(32)) multiplexer_2 (.in0(WriteData), .in1(ImmExtD), .out(SrcBE), .sel(ALUSrcBE));
  Adder #(.width(32)) adder_2 (.a(PC), .b(ImmExtD), .out(PCTargetE));  // open: cin, cout
  // Probe on RD1D
  // Probe on SrcBE
  // Probe on ALUControlD
  // Probe on ZeroE
  alu alu_1 (.SrcA(RD1D), .SrcB(SrcBE), .ALUControl(ALUControlD), .Zero(ZeroE), .ALUResult(MemAddr));
  // Probe on MemAddr
  // Probe on MemAddr
  // Probe on WriteData
  // Probe on Instr[11:7]
  // Probe on PCPlus4D
  // Probe on RegWriteD
  // Probe on RegWriteD
  // Probe on ResultSrcD
  // Probe on ResultSrcD
  // Probe on MemWrite
  // Probe on MemWrite
  // Probe on MemAddr
  // Probe on WriteData
  // Probe on Instr[11:7]
  // Probe on PCPlus4D
  // Probe on MemWrite
  // Probe on RegWriteD
  // Probe on RegWriteD
  // Probe on ResultSrcD
  // Probe on ResultSrcD
  // Probe on MemAddr
  // Probe on ReadData
  // Probe on Instr[11:7]
  // Probe on PCPlus4D
  // Probe on MemAddr
  // Probe on ReadData
  // Probe on Instr[11:7]
  // Probe on PCPlus4D
  // Probe on ResultSrcD
  Multiplexer #(.select(2), .width(32)) multiplexer_3 (
    .in0(MemAddr), .in1(ReadData), .in2(PCPlus4D), .out(ResultW), .sel(ResultSrcD));  // open: in3
  // Probe on ResultW

  // Other names for the same wires on the sheet: ALUControlE[2:0] = ALUControlD; ALUResultE[31:0] = MemAddr;
  //   ALUResultM[31:0] = MemAddr; ALUResultW[31:0] = MemAddr; ALUSrcD = ALUSrcBE; BranchE = BranchD;
  //   ImmExtE[31:0] = ImmExtD; Imm[31:0] = Instr; InstrD[31:0] = Instr; InstrF[31:0] = Instr;
  //   opcode[6:0] = Instr[6:0]; RdD[4:0] = Instr[11:7]; RdE[4:0] = Instr[11:7]; RdM[4:0] = Instr[11:7];
  //   RdW[4:0] = Instr[11:7]; funct3[2:0] = Instr[14:12]; Rs1D[4:0] = Instr[19:15]; Rs1E[4:0] = Instr[19:15];
  //   Rs2D[4:0] = Instr[24:20]; Rs2E[4:0] = Instr[24:20]; funct7_5 = Instr[30]; JumpE = JumpD; MemWriteD = MemWrite;
  //   MemWriteE = MemWrite; MemWriteM = MemWrite; PCD[31:0] = PC; PCE[31:0] = PC; PCF[31:0] = PC;
  //   PCPlus4E[31:0] = PCPlus4D; PCPlus4F[31:0] = PCPlus4D; PCPlus4M[31:0] = PCPlus4D; PCPlus4W[31:0] = PCPlus4D;
  //   ReadDataM[31:0] = ReadData; ReadDataW[31:0] = ReadData; RegWriteE = RegWriteD; RegWriteM = RegWriteD;
  //   RegWriteW = RegWriteD; ResultSrcE[1:0] = ResultSrcD; ResultSrcM[1:0] = ResultSrcD; ResultSrcW[1:0] = ResultSrcD;
  //   RD1E[31:0] = RD1D; SrcAE[31:0] = RD1D; RD2D[31:0] = WriteData; RD2E[31:0] = WriteData;
  //   WriteDataE[31:0] = WriteData; WriteDataM[31:0] = WriteData

  // Notes on the sheet:
  //   PC
  //   Fetch
  //   Control Unit
  //   Decode
  //   Execute
  //   Memory
  //   Writeback
endmodule

module memory (
  input  CLK,
  input  WE,
  input  [31:0] A,
  input  [31:0] WD,
  output [31:0] ReadData
);

  // Probe on A[25:2]
  RAM #(.addrWidth(24), .asyncread("true"), .dataWidth(32)) ram_1 (
    .addr(A[25:2]), .we(WE), .oe(1'b1), .clk(CLK), .din(WD), .dout(ReadData));

  // Other names for the same wires on the sheet: A_t[23:0] = A[25:2]
endmodule

module reg1 (
  input  in_1,
  input  WE,
  input  CLK,
  input  CLR,
  output out_5
);

  Register #(.width(1)) register_1 (.D(in_1), .en(WE), .clk(CLK), .Q(out_5), .clr(CLR));
endmodule

module reg2 (
  input  [1:0] in_1,
  input  WE,
  input  CLK,
  input  CLR,
  output [1:0] out_5
);

  Register #(.width(2)) register_1 (.D(in_1), .en(WE), .clk(CLK), .Q(out_5), .clr(CLR));
endmodule

module reg3 (
  input  [2:0] in_1,
  input  WE,
  input  CLK,
  input  CLR,
  output [2:0] out_5
);

  Register #(.width(3)) register_1 (.D(in_1), .en(WE), .clk(CLK), .Q(out_5), .clr(CLR));
endmodule

module reg5 (
  input  [4:0] in_1,
  input  WE,
  input  CLK,
  input  CLR,
  output [4:0] out_5
);

  Register #(.width(5)) register_1 (.D(in_1), .en(WE), .clk(CLK), .Q(out_5), .clr(CLR));
endmodule

module reg32 (
  input  [31:0] in_1,
  input  WE,
  input  CLK,
  input  CLR,
  output [31:0] out_5
);

  Register #(.width(32)) register_1 (.D(in_1), .en(WE), .clk(CLK), .Q(out_5), .clr(CLR));
endmodule

module regfile (
  input  [4:0] A1,
  input  [4:0] A2,
  input  [4:0] A3,
  input  [31:0] WD3,
  input  WE3,
  input  CLK,
  output [31:0] RD1,
  output [31:0] RD2
);

  wire w0, w1, w2, w3, w4, w5, w6, w7, w8, w9, w10, w11, w12, w13, w14, w15, w16, w17, w18, w19, w20, w21,
       w22, w23, w24, w25, w26, w27, w28, w29, w30, w31, wr0, wr1, wr2, wr3, wr4, wr5, wr6, wr7, wr8, wr9,
       wr10, wr11, wr12, wr13, wr14, wr15, wr16, wr17, wr18, wr19, wr20, wr21, wr22, wr23, wr24, wr25, wr26,
       wr27, wr28, wr29, wr30, wr31;
  wire [31:0] o0, o1, o2, o3, o4, o5, o6, o7, o8, o9, o10, o11, o12, o13, o14, o15, o16, o17, o18, o19, o20,
       o21, o22, o23, o24, o25, o26, o27, o28, o29, o30, o31;

  Decoder #(.select(5)) decoder_1 (
    .out0(wr0), .out1(wr1), .out2(wr2), .out3(wr3), .out4(wr4), .out5(wr5), .out6(wr6), .out7(wr7),
    .out8(wr8), .out9(wr9), .out10(wr10), .out11(wr11), .out12(wr12), .out13(wr13), .out14(wr14),
    .out15(wr15), .out16(wr16), .out17(wr17), .out18(wr18), .out19(wr19), .out20(wr20), .out21(wr21),
    .out22(wr22), .out23(wr23), .out24(wr24), .out25(wr25), .out26(wr26), .out27(wr27), .out28(wr28),
    .out29(wr29), .out30(wr30), .out31(wr31), .sel(A3));  // open: en
  Register #(.width(32)) x0 (.D(WD3), .en(w0), .clk(CLK), .Q(o0), .clr(1'b1));
  Register #(.width(32)) x1 (.D(WD3), .en(w1), .clk(CLK), .Q(o1), .clr(1'b0));
  Register #(.width(32)) x2 (.D(WD3), .en(w2), .clk(CLK), .Q(o2), .clr(1'b0));
  Register #(.width(32)) x3 (.D(WD3), .en(w3), .clk(CLK), .Q(o3), .clr(1'b0));
  Register #(.width(32)) x4 (.D(WD3), .en(w4), .clk(CLK), .Q(o4), .clr(1'b0));
  Register #(.width(32)) x5 (.D(WD3), .en(w5), .clk(CLK), .Q(o5), .clr(1'b0));
  Register #(.width(32)) x6 (.D(WD3), .en(w6), .clk(CLK), .Q(o6), .clr(1'b0));
  Register #(.width(32)) x7 (.D(WD3), .en(w7), .clk(CLK), .Q(o7), .clr(1'b0));
  Register #(.width(32)) x8 (.D(WD3), .en(w8), .clk(CLK), .Q(o8), .clr(1'b0));
  Register #(.width(32)) x9 (.D(WD3), .en(w9), .clk(CLK), .Q(o9), .clr(1'b0));
  Register #(.width(32)) x10 (.D(WD3), .en(w10), .clk(CLK), .Q(o10), .clr(1'b0));
  Register #(.width(32)) x11 (.D(WD3), .en(w11), .clk(CLK), .Q(o11), .clr(1'b0));
  Register #(.width(32)) x12 (.D(WD3), .en(w12), .clk(CLK), .Q(o12), .clr(1'b0));
  Register #(.width(32)) x13 (.D(WD3), .en(w13), .clk(CLK), .Q(o13), .clr(1'b0));
  Register #(.width(32)) x14 (.D(WD3), .en(w14), .clk(CLK), .Q(o14), .clr(1'b0));
  Register #(.width(32)) x15 (.D(WD3), .en(w15), .clk(CLK), .Q(o15), .clr(1'b0));
  Register #(.width(32)) x16 (.D(WD3), .en(w16), .clk(CLK), .Q(o16), .clr(1'b0));
  Register #(.width(32)) x17 (.D(WD3), .en(w17), .clk(CLK), .Q(o17), .clr(1'b0));
  Register #(.width(32)) x18 (.D(WD3), .en(w18), .clk(CLK), .Q(o18), .clr(1'b0));
  Register #(.width(32)) x19 (.D(WD3), .en(w19), .clk(CLK), .Q(o19), .clr(1'b0));
  Register #(.width(32)) x20 (.D(WD3), .en(w20), .clk(CLK), .Q(o20), .clr(1'b0));
  Register #(.width(32)) x21 (.D(WD3), .en(w21), .clk(CLK), .Q(o21), .clr(1'b0));
  Register #(.width(32)) x22 (.D(WD3), .en(w22), .clk(CLK), .Q(o22), .clr(1'b0));
  Register #(.width(32)) x23 (.D(WD3), .en(w23), .clk(CLK), .Q(o23), .clr(1'b0));
  and and_1 (w0, wr0, WE3);
  and and_2 (w1, wr1, WE3);
  and and_3 (w2, wr2, WE3);
  and and_4 (w3, wr3, WE3);
  and and_5 (w4, wr4, WE3);
  and and_6 (w5, wr5, WE3);
  and and_7 (w6, wr6, WE3);
  and and_8 (w7, wr7, WE3);
  Register #(.width(32)) x24 (.D(WD3), .en(w24), .clk(CLK), .Q(o24), .clr(1'b0));
  Register #(.width(32)) x25 (.D(WD3), .en(w25), .clk(CLK), .Q(o25), .clr(1'b0));
  Register #(.width(32)) x26 (.D(WD3), .en(w26), .clk(CLK), .Q(o26), .clr(1'b0));
  Register #(.width(32)) x27 (.D(WD3), .en(w27), .clk(CLK), .Q(o27), .clr(1'b0));
  Register #(.width(32)) x28 (.D(WD3), .en(w28), .clk(CLK), .Q(o28), .clr(1'b0));
  Register #(.width(32)) x29 (.D(WD3), .en(w29), .clk(CLK), .Q(o29), .clr(1'b0));
  Register #(.width(32)) x30 (.D(WD3), .en(w30), .clk(CLK), .Q(o30), .clr(1'b0));
  Register #(.width(32)) x31 (.D(WD3), .en(w31), .clk(CLK), .Q(o31), .clr(1'b0));
  and and_9 (w8, wr8, WE3);
  and and_10 (w9, wr9, WE3);
  and and_11 (w10, wr10, WE3);
  and and_12 (w11, wr11, WE3);
  and and_13 (w12, wr12, WE3);
  and and_14 (w13, wr13, WE3);
  and and_15 (w14, wr14, WE3);
  and and_16 (w15, wr15, WE3);
  and and_17 (w16, wr16, WE3);
  and and_18 (w17, wr17, WE3);
  and and_19 (w18, wr18, WE3);
  and and_20 (w19, wr19, WE3);
  and and_21 (w20, wr20, WE3);
  and and_22 (w21, wr21, WE3);
  and and_23 (w22, wr22, WE3);
  and and_24 (w23, wr23, WE3);
  and and_25 (w24, wr24, WE3);
  and and_26 (w25, wr25, WE3);
  and and_27 (w26, wr26, WE3);
  and and_28 (w27, wr27, WE3);
  and and_29 (w28, wr28, WE3);
  and and_30 (w29, wr29, WE3);
  and and_31 (w30, wr30, WE3);
  and and_32 (w31, wr31, WE3);
  Multiplexer #(.enable("true"), .select(5), .width(32)) multiplexer_1 (
    .in0(o0), .in1(o1), .in2(o2), .in3(o3), .in4(o4), .in5(o5), .in6(o6), .in7(o7), .in8(o8), .in9(o9),
    .in10(o10), .in11(o11), .in12(o12), .in13(o13), .in14(o14), .in15(o15), .in16(o16), .in17(o17),
    .in18(o18), .in19(o19), .in20(o20), .in21(o21), .in22(o22), .in23(o23), .in24(o24), .in25(o25),
    .in26(o26), .in27(o27), .in28(o28), .in29(o29), .in30(o30), .in31(o31), .out(RD1), .sel(A1));  // open: en
  Multiplexer #(.enable("true"), .select(5), .width(32)) multiplexer_2 (
    .in0(o0), .in1(o1), .in2(o2), .in3(o3), .in4(o4), .in5(o5), .in6(o6), .in7(o7), .in8(o8), .in9(o9),
    .in10(o10), .in11(o11), .in12(o12), .in13(o13), .in14(o14), .in15(o15), .in16(o16), .in17(o17),
    .in18(o18), .in19(o19), .in20(o20), .in21(o21), .in22(o22), .in23(o23), .in24(o24), .in25(o25),
    .in26(o26), .in27(o27), .in28(o28), .in29(o29), .in30(o30), .in31(o31), .out(RD2), .sel(A2));  // open: en
endmodule

module extend (
  input  [31:0] Instr,
  input  [2:0] ImmSrc,
  output [31:0] ImmExt
);

  wire [31:0] BTypeImm, ITypeImm, JTypeImm, STypeImm, UTypeImm;

  // Probe on ITypeImm
  assign ITypeImm = {{20{Instr[31]}}, Instr[31:20]};  // Bit_Extender bit_extender_1
  // Probe on BTypeImm
  assign BTypeImm = {{19{Instr[31]}}, {Instr[31], Instr[7], Instr[30:25], Instr[11:8], 1'b0}};  // Bit_Extender bit_extender_2
  // Probe on JTypeImm
  assign JTypeImm = {{11{Instr[31]}}, {Instr[31], Instr[19:12], Instr[20], Instr[30:21], 1'b0}};  // Bit_Extender bit_extender_3
  assign STypeImm = {{20{Instr[31]}}, {Instr[31:25], Instr[11:7]}};  // Bit_Extender bit_extender_4
  Multiplexer #(.enable("true"), .select(3), .width(32)) multiplexer_1 (
    .in0(ITypeImm), .in1(STypeImm), .in2(BTypeImm), .in3(JTypeImm), .in4(UTypeImm), .out(ImmExt), .sel(ImmSrc));  // open: in5, in6, in7, en
  // Probe on STypeImm
  // Probe on UTypeImm
  assign UTypeImm = {{12{Instr[31]}}, Instr[31:12]};  // Bit_Extender bit_extender_5

  // Other names for the same wires on the sheet: ITypeImm12[11:0] = Instr[31:20];
  //   JTypeImm21[20:1] = {Instr[31], Instr[19:12], Instr[20], Instr[30:21]}; UTypeImm20[19:0] = Instr[31:12];
  //   BTypeImm13[12:1] = {Instr[31], Instr[7], Instr[30:25], Instr[11:8]};
  //   STypeImm12[11:0] = {Instr[31:25], Instr[11:7]}

  // Notes on the sheet:
  //   I-type
  //   Input
  //   B-type
  //   J-type
  //   Output
  //   S-type
  //   U-type
endmodule

module alu (
  input  [31:0] SrcA,
  input  [31:0] SrcB,
  input  [2:0] ALUControl,
  output Zero,
  output [31:0] ALUResult
);

  wire comparator_1_lt, or_2_out;
  wire [31:0] adder_1_out, and_1_out, bit_extender_1_out, or_1_out, shifter_1_out, subtractor_1_out;

  Adder #(.width(32)) adder_1 (.a(SrcA), .b(SrcB), .out(adder_1_out));  // open: cin, cout
  Subtractor #(.width(32)) subtractor_1 (.a(SrcA), .b(SrcB), .out(subtractor_1_out));  // open: bin, bout
  assign and_1_out = SrcA & SrcB;  // AND_Gate and_1, 32 bits wide
  assign or_1_out = SrcA | SrcB;  // OR_Gate or_1, 32 bits wide
  Shifter #(.width(32)) shifter_1 (.in(SrcA), .\dist (SrcB[4:0]), .out(shifter_1_out));
  Comparator #(.mode("unsigned"), .width(32)) comparator_1 (.a(SrcA), .b(SrcB), .lt(comparator_1_lt));  // open: gt, eq
  assign bit_extender_1_out = {{31{1'b0}}, comparator_1_lt};  // Bit_Extender bit_extender_1
  Multiplexer #(.enable("true"), .select(3), .width(32)) multiplexer_1 (
    .in0(adder_1_out), .in1(subtractor_1_out), .in2(and_1_out), .in3(or_1_out), .in4(shifter_1_out),
    .in5(bit_extender_1_out), .out(ALUResult), .sel(ALUControl));  // open: in6, in7, en
  // Probe on ALUControl
  or or_2 (or_2_out, ALUResult[0], ALUResult[1], ALUResult[2], ALUResult[3], ALUResult[4], ALUResult[5], ALUResult[6], ALUResult[7], ALUResult[8], ALUResult[9], ALUResult[10], ALUResult[11], ALUResult[12], ALUResult[13], ALUResult[14], ALUResult[15], ALUResult[17], ALUResult[18], ALUResult[19], ALUResult[20], ALUResult[21], ALUResult[22], ALUResult[23], ALUResult[24], ALUResult[25], ALUResult[26], ALUResult[27], ALUResult[28], ALUResult[29], ALUResult[30], ALUResult[31], ALUResult[16]);
  not not_1 (Zero, or_2_out);

  // Notes on the sheet:
  //   Input
  //   ALUResult
  //   Output
  //   Zero
endmodule

module instrdecoder (
  input  [6:0] opcode,
  output [2:0] ImmSrc
);

  wire IsBEQ, IsITypeALU, IsJAL, IsLW, IsRType, IsSW;
  wire [2:0] Selector, undriven;

  Comparator #(.mode("unsigned"), .width(7)) comparator_1 (.a(opcode), .b(7'b0000011), .eq(IsLW));  // open: gt, lt
  Comparator #(.mode("unsigned"), .width(7)) comparator_2 (.a(opcode), .b(7'b0100011), .eq(IsSW));  // open: gt, lt
  Comparator #(.mode("unsigned"), .width(7)) comparator_3 (.a(opcode), .b(7'b0110011), .eq(IsRType));  // open: gt, lt
  Comparator #(.mode("unsigned"), .width(7)) comparator_4 (.a(opcode), .b(7'b1100011), .eq(IsBEQ));  // open: gt, lt
  Comparator #(.mode("unsigned"), .width(7)) comparator_5 (
    .a(opcode), .b(7'b0010011), .eq(IsITypeALU));  // open: gt, lt
  Comparator #(.mode("unsigned"), .width(7)) comparator_6 (.a(opcode), .b(7'b1101111), .eq(IsJAL));  // open: gt, lt
  Priority_Encoder priority_encoder_1 (
    .in0(IsLW), .in1(IsSW), .in2(IsRType), .in3(IsBEQ), .in4(IsITypeALU), .in5(IsJAL), .out(Selector));  // open: in6, in7, en_in, gs, en_out
  // Probe on Selector
  Multiplexer #(.enable("true"), .select(3), .width(3)) multiplexer_1 (
    .in0(3'b000), .in1(3'b001), .in2(undriven), .in3(3'b010), .in4(3'b000), .in5(3'b011), .out(ImmSrc),
    .sel(Selector));  // open: in6, in7, en
endmodule

module instmem (
  input  [31:0] Address,
  output [31:0] Instr
);

  ROM #(.dataWidth(32)) rom_1 (.addr(Address[9:2]), .data(Instr));

  // Notes on the sheet:
  //   // Nasty hack to make word-addressable ROM usable
  //   contents of rom_1 (hex, n*v repeats v):
  //   30000513 30100593 70000093 15a023
endmodule

module controlunit (
  input  [6:0] opcode,
  input  [2:0] funct3,
  input  funct7_5,
  output RegWrite,
  output [1:0] ResultSrc,
  output MemWrite,
  output Jump,
  output Branch,
  output [2:0] ALUControl,
  output ALUSrc,
  output [2:0] ImmSrc
);

  wire IsSupported;
  wire [1:0] ALUOp;

  maindecoder maindecoder_1 (
    .opcode(opcode), .IsSupported(IsSupported), .Branch(Branch), .ResultSrc(ResultSrc), .MemWrite(MemWrite),
    .ALUSrc(ALUSrc), .ImmSrc(ImmSrc), .RegWrite(RegWrite), .ALUOp(ALUOp), .Jump(Jump));
  aludecoder aludecoder_1 (
    .funct7_5(funct7_5), .funct3(funct3), .ALUOp(ALUOp), .opcode(opcode), .ALUControl(ALUControl));
  // Probe on Branch
  // Probe on ResultSrc
  // Probe on MemWrite
  // Probe on ALUSrc
  // Probe on ImmSrc
  // Probe on RegWrite
  // Probe on ALUOp
  // Probe on Jump
  LED led_1 (.in(IsSupported));
endmodule

module maindecoder (
  input  [6:0] opcode,
  output IsSupported,
  output Branch,
  output [1:0] ResultSrc,
  output MemWrite,
  output ALUSrc,
  output [2:0] ImmSrc,
  output RegWrite,
  output [1:0] ALUOp,
  output Jump
);

  wire IsBEQ, IsITypeALU, IsJAL, IsLW, IsRType, IsSpecial, IsSW, priority_encoder_1_en_out;
  wire [1:0] undriven, undriven_2, undriven_3;
  wire [2:0] Selector, undriven_4;

  Comparator #(.mode("unsigned"), .width(7)) comparator_1 (.a(opcode), .b(7'b0000011), .eq(IsLW));  // open: gt, lt
  Comparator #(.mode("unsigned"), .width(7)) comparator_2 (.a(opcode), .b(7'b0100011), .eq(IsSW));  // open: gt, lt
  Comparator #(.mode("unsigned"), .width(7)) comparator_3 (.a(opcode), .b(7'b0110011), .eq(IsRType));  // open: gt, lt
  Comparator #(.mode("unsigned"), .width(7)) comparator_4 (.a(opcode), .b(7'b1100011), .eq(IsBEQ));  // open: gt, lt
  Comparator #(.mode("unsigned"), .width(7)) comparator_5 (
    .a(opcode), .b(7'b0010011), .eq(IsITypeALU));  // open: gt, lt
  Comparator #(.mode("unsigned"), .width(7)) comparator_6 (.a(opcode), .b(7'b1101111), .eq(IsJAL));  // open: gt, lt
  Comparator #(.mode("unsigned"), .width(7)) comparator_7 (.a(opcode), .b({7{1'b0}}), .eq(IsSpecial));  // open: gt, lt
  Priority_Encoder priority_encoder_1 (
    .in0(IsLW), .in1(IsSW), .in2(IsRType), .in3(IsBEQ), .in4(IsITypeALU), .in5(IsJAL), .in6(IsSpecial),
    .out(Selector), .en_out(priority_encoder_1_en_out));  // open: in7, en_in, gs
  not not_1 (IsSupported, priority_encoder_1_en_out);
  // Probe on Selector
  Multiplexer #(.enable("true"), .select(3)) multiplexer_1 (
    .in0(1'b1), .in1(1'b0), .in2(1'b1), .in3(1'b0), .in4(1'b1), .in5(1'b1), .in6(1'b0), .out(RegWrite),
    .sel(Selector));  // open: in7, en
  Multiplexer #(.enable("true"), .select(3)) multiplexer_2 (
    .in0(1'b1), .in1(1'b1), .in2(1'b0), .in3(1'b0), .in4(1'b1), .in5(1'b1), .in6(1'b0), .out(ALUSrc),
    .sel(Selector));  // open: in7, en
  // Probe on ResultSrc
  Multiplexer #(.enable("true"), .select(3), .width(2)) multiplexer_3 (
    .in0(2'b01), .in1(undriven), .in2(2'b00), .in3(undriven_2), .in4(2'b00), .in5(2'b10), .in6(2'b00),
    .out(ResultSrc), .sel(Selector));  // open: in7, en
  // Probe on Selector
  Multiplexer #(.enable("true"), .select(3), .width(2)) multiplexer_4 (
    .in0(2'b00), .in1(2'b00), .in2(2'b10), .in3(2'b01), .in4(2'b10), .in5(undriven_3), .in6(2'b00),
    .out(ALUOp), .sel(Selector));  // open: in7, en
  Multiplexer #(.enable("true"), .select(3), .width(3)) multiplexer_5 (
    .in0(3'b000), .in1(3'b001), .in2(undriven_4), .in3(3'b010), .in4(3'b000), .in5(3'b011), .in6(3'b000),
    .out(ImmSrc), .sel(Selector));  // open: in7, en
  Multiplexer #(.enable("true"), .select(3)) multiplexer_6 (
    .in0(1'b0), .in1(1'b1), .in2(1'b0), .in3(1'b0), .in4(1'b0), .in5(1'b0), .in6(1'b0), .out(MemWrite),
    .sel(Selector));  // open: in7, en
  Multiplexer #(.enable("true"), .select(3)) multiplexer_7 (
    .in0(1'b0), .in1(1'b0), .in2(1'b0), .in3(1'b1), .in4(1'b0), .in5(1'b0), .in6(1'b0), .out(Branch),
    .sel(Selector));  // open: in7, en
  Multiplexer #(.enable("true"), .select(3)) multiplexer_8 (
    .in0(1'b0), .in1(1'b0), .in2(1'b0), .in3(1'b0), .in4(1'b0), .in5(1'b1), .in6(1'b0), .out(Jump),
    .sel(Selector));  // open: in7, en

  // Notes on the sheet:
  //   Input
  //   Helpers
  //   Output
  //   Control Signals
endmodule

module aludecoder (
  input  funct7_5,
  input  [2:0] funct3,
  input  [1:0] ALUOp,
  input  [6:0] opcode,
  output [2:0] ALUControl
);

  wire and_1_out, and_2_out, comparator_1_eq, comparator_2_eq, comparator_3_eq, comparator_4_eq,
       comparator_5_eq, comparator_6_eq, comparator_7_eq, comparator_8_eq, comparator_9_eq, comparator_10_eq,
       comparator_11_eq, comparator_12_eq, comparator_13_eq, comparator_14_eq, comparator_15_eq,
       comparator_16_eq, IsAdd, IsAnd, IsOr, IsSll, IsSLT, IsSub, not_1_out;

  Priority_Encoder priority_encoder_1 (
    .in0(IsAdd), .in1(IsSub), .in2(IsAnd), .in3(IsOr), .in4(IsSll), .in5(IsSLT), .out(ALUControl));  // open: in6, in7, en_in, gs, en_out
  Comparator #(.mode("unsigned"), .width(2)) comparator_1 (.a(ALUOp), .b(2'b00), .eq(comparator_1_eq));  // open: gt, lt
  Comparator #(.mode("unsigned"), .width(2)) comparator_2 (.a(ALUOp), .b(2'b10), .eq(comparator_2_eq));  // open: gt, lt
  Comparator #(.mode("unsigned"), .width(3)) comparator_3 (
    .a(funct3), .b(3'b000), .eq(comparator_3_eq));  // open: gt, lt
  not not_1 (not_1_out, comparator_4_eq);
  Comparator #(.mode("unsigned"), .width(2)) comparator_4 (
    .a({opcode[5], funct7_5}), .b(2'b11), .eq(comparator_4_eq));  // open: gt, lt
  Comparator #(.mode("unsigned"), .width(2)) comparator_5 (.a(ALUOp), .b(2'b01), .eq(comparator_5_eq));  // open: gt, lt
  Comparator #(.mode("unsigned"), .width(2)) comparator_6 (.a(ALUOp), .b(2'b10), .eq(comparator_6_eq));  // open: gt, lt
  Comparator #(.mode("unsigned"), .width(3)) comparator_7 (
    .a(funct3), .b(3'b000), .eq(comparator_7_eq));  // open: gt, lt
  Comparator #(.mode("unsigned"), .width(2)) comparator_8 (
    .a({opcode[5], funct7_5}), .b(2'b11), .eq(comparator_8_eq));  // open: gt, lt
  Comparator #(.mode("unsigned"), .width(2)) comparator_9 (.a(ALUOp), .b(2'b10), .eq(comparator_9_eq));  // open: gt, lt
  Comparator #(.mode("unsigned"), .width(3)) comparator_10 (
    .a(funct3), .b(3'b010), .eq(comparator_10_eq));  // open: gt, lt
  Comparator #(.mode("unsigned"), .width(2)) comparator_11 (
    .a(ALUOp), .b(2'b10), .eq(comparator_11_eq));  // open: gt, lt
  Comparator #(.mode("unsigned"), .width(3)) comparator_12 (
    .a(funct3), .b(3'b110), .eq(comparator_12_eq));  // open: gt, lt
  Comparator #(.mode("unsigned"), .width(2)) comparator_13 (
    .a(ALUOp), .b(2'b10), .eq(comparator_13_eq));  // open: gt, lt
  Comparator #(.mode("unsigned"), .width(3)) comparator_14 (
    .a(funct3), .b(3'b111), .eq(comparator_14_eq));  // open: gt, lt
  Comparator #(.mode("unsigned"), .width(2)) comparator_15 (
    .a(ALUOp), .b(2'b10), .eq(comparator_15_eq));  // open: gt, lt
  Comparator #(.mode("unsigned"), .width(3)) comparator_16 (
    .a(funct3), .b(3'b001), .eq(comparator_16_eq));  // open: gt, lt
  and and_1 (and_1_out, comparator_2_eq, comparator_3_eq, not_1_out);
  or or_1 (IsSub, comparator_5_eq, and_2_out);
  and and_2 (and_2_out, comparator_6_eq, comparator_7_eq, comparator_8_eq);
  and and_3 (IsSLT, comparator_9_eq, comparator_10_eq);
  and and_4 (IsOr, comparator_11_eq, comparator_12_eq);
  and and_5 (IsAnd, comparator_13_eq, comparator_14_eq);
  and and_6 (IsSll, comparator_15_eq, comparator_16_eq);
  or or_2 (IsAdd, comparator_1_eq, and_1_out);

  // Other names for the same wires on the sheet: concat[1:0] = {opcode[5], funct7_5}; opcode_5 = opcode[5]
endmodule
